# Fritzing sketch Home Automation-Schematics (saved by Fritzing 0.9.3b)
breadboards: 1

parts:
  KY-1 = Keyes Relay [package=THT]
  Part1 = Arduino Uno (Rev3)
  Part2 = Bluetooth HC-05 Macho
  KY-3 = Keyes Relay [package=THT]
  R1 = Resistor [tolerance=±5% resistance=1k package=THT]
  R2 = Resistor [tolerance=±5% resistance=2.2k package=THT]
  R3 = Photocell (LDR) [package=THT]
  R4 = Resistor [tolerance=±5% resistance=2.2k package=THT]  # not connected
  J1 = Basic Servo

nets:
  N1: KY-1.signal, Part1.D12/MISO
  VCC: KY-1.power, Part1.5V, Part2.VCC, KY-3.power, J1.vcc
  GND: KY-1.ground, Part1.A0, Part1.GND, Part2.GND, KY-3.ground, R2.Pin_1, R3.pin_1, J1.gnd
  N2: Part1.D9_PWM, J1.pulse
  N3: Part1.D13/SCK, KY-3.signal
  N4: Part1.D0/RX, Part2.TXD
  N5: Part1.D1/TX, R1.Pin_1
  N6: Part2.RXD, R1.Pin_0, R2.Pin_0

custom parts:
  Keyes Relay: The Keyes 5V relay module is suitable for SCM development, home appliance control. It uses a 5V~12V TIL control signal which can control DC / AC signal.
