# Fritzing sketch hc 05 connection (saved by Fritzing 0.9.3b)

parts:
  Part1 = Arduino Uno (Rev3)
  Part2 = Bluetooth HC-05 Macho
  R1 = Resistor [tolerance=±5% resistance=1k package=THT]
  R2 = Resistor [tolerance=±5% resistance=2.2k package=THT]

nets:
  N1: Part1.D0/RX, Part2.TXD
  N2: Part1.D1/TX, R1.Pin_1
  5V: Part1.5V, Part2.VCC
  GND: Part1.GND, Part2.GND, R2.Pin_0
  N3: Part2.RXD, R2.Pin_1
